// Logisim project microp proje.circ as structural Verilog: 33 circuits, main circuit 16-bit Register (SR)
module _16_bit_Register__SR (
  input  [15:0] in_1,
  input  Load,
  input  Clock,
  output [15:0] Output
);

  wire and_1_out, and_2_out, and_3_out, and_4_out, and_5_out, and_6_out, and_7_out, and_8_out, and_9_out,
       and_10_out, and_11_out, and_12_out, and_13_out, and_14_out, and_15_out, and_16_out, and_17_out,
       and_18_out, and_19_out, and_20_out, and_21_out, and_22_out, and_23_out, and_24_out, and_25_out,
       and_26_out, and_27_out, and_28_out, and_29_out, and_30_out, and_31_out, and_32_out;

  and and_1 (and_1_out, in_1[0], Load);
  and and_2 (and_2_out, ~in_1[0], Load);  // AND_Gate
  and and_3 (and_3_out, in_1[1], Load);
  and and_4 (and_4_out, ~in_1[1], Load);  // AND_Gate
  and and_5 (and_5_out, in_1[2], Load);
  and and_6 (and_6_out, ~in_1[2], Load);  // AND_Gate
  and and_7 (and_7_out, in_1[3], Load);
  and and_8 (and_8_out, ~in_1[3], Load);  // AND_Gate
  and and_9 (and_9_out, in_1[4], Load);
  and and_10 (and_10_out, ~in_1[4], Load);  // AND_Gate
  and and_11 (and_11_out, in_1[5], Load);
  and and_12 (and_12_out, ~in_1[5], Load);  // AND_Gate
  and and_13 (and_13_out, in_1[6], Load);
  and and_14 (and_14_out, ~in_1[6], Load);  // AND_Gate
  and and_15 (and_15_out, in_1[7], Load);
  and and_16 (and_16_out, ~in_1[7], Load);  // AND_Gate
  and and_17 (and_17_out, in_1[8], Load);
  and and_18 (and_18_out, ~in_1[8], Load);  // AND_Gate
  and and_19 (and_19_out, in_1[9], Load);
  and and_20 (and_20_out, ~in_1[9], Load);  // AND_Gate
  and and_21 (and_21_out, in_1[10], Load);
  and and_22 (and_22_out, ~in_1[10], Load);  // AND_Gate
  and and_23 (and_23_out, in_1[11], Load);
  and and_24 (and_24_out, ~in_1[11], Load);  // AND_Gate
  and and_25 (and_25_out, in_1[12], Load);
  and and_26 (and_26_out, ~in_1[12], Load);  // AND_Gate
  and and_27 (and_27_out, in_1[13], Load);
  and and_28 (and_28_out, ~in_1[13], Load);  // AND_Gate
  and and_29 (and_29_out, in_1[14], Load);
  and and_30 (and_30_out, ~in_1[14], Load);  // AND_Gate
  and and_31 (and_31_out, in_1[15], Load);
  and and_32 (and_32_out, ~in_1[15], Load);  // AND_Gate
  S_R_Flip_Flop s_r_ff_1 (.S(and_1_out), .clk(Clock), .R(and_2_out), .Q(Output[0]));  // open: Qn, preset, reset, en
  S_R_Flip_Flop s_r_ff_2 (.S(and_3_out), .clk(Clock), .R(and_4_out), .Q(Output[1]));  // open: Qn, preset, reset, en
  S_R_Flip_Flop s_r_ff_3 (.S(and_5_out), .clk(Clock), .R(and_6_out), .Q(Output[2]));  // open: Qn, preset, reset, en
  S_R_Flip_Flop s_r_ff_4 (.S(and_7_out), .clk(Clock), .R(and_8_out), .Q(Output[3]));  // open: Qn, preset, reset, en
  S_R_Flip_Flop s_r_ff_5 (.S(and_9_out), .clk(Clock), .R(and_10_out), .Q(Output[4]));  // open: Qn, preset, reset, en
  S_R_Flip_Flop s_r_ff_6 (.S(and_11_out), .clk(Clock), .R(and_12_out), .Q(Output[5]));  // open: Qn, preset, reset, en
  S_R_Flip_Flop s_r_ff_7 (.S(and_13_out), .clk(Clock), .R(and_14_out), .Q(Output[6]));  // open: Qn, preset, reset, en
  S_R_Flip_Flop s_r_ff_8 (.S(and_15_out), .clk(Clock), .R(and_16_out), .Q(Output[7]));  // open: Qn, preset, reset, en
  S_R_Flip_Flop s_r_ff_9 (.S(and_17_out), .clk(Clock), .R(and_18_out), .Q(Output[8]));  // open: Qn, preset, reset, en
  S_R_Flip_Flop s_r_ff_10 (.S(and_19_out), .clk(Clock), .R(and_20_out), .Q(Output[9]));  // open: Qn, preset, reset, en
  S_R_Flip_Flop s_r_ff_11 (.S(and_21_out), .clk(Clock), .R(and_22_out), .Q(Output[10]));  // open: Qn, preset, reset, en
  S_R_Flip_Flop s_r_ff_12 (.S(and_23_out), .clk(Clock), .R(and_24_out), .Q(Output[11]));  // open: Qn, preset, reset, en
  S_R_Flip_Flop s_r_ff_13 (.S(and_25_out), .clk(Clock), .R(and_26_out), .Q(Output[12]));  // open: Qn, preset, reset, en
  S_R_Flip_Flop s_r_ff_14 (.S(and_27_out), .clk(Clock), .R(and_28_out), .Q(Output[13]));  // open: Qn, preset, reset, en
  S_R_Flip_Flop s_r_ff_15 (.S(and_29_out), .clk(Clock), .R(and_30_out), .Q(Output[14]));  // open: Qn, preset, reset, en
  S_R_Flip_Flop s_r_ff_16 (.S(and_31_out), .clk(Clock), .R(and_32_out), .Q(Output[15]));  // open: Qn, preset, reset, en
endmodule

module _16_bit_Register_with_increment (
  input  [15:0] in_1,
  input  [15:0] in_2,
  input  in_3,
  input  in_4,
  input  [7:0] in_5,
  output [15:0] out_6
);

  wire n16_bit_register_sr_1_p3, or_1_out;
  wire [15:0] adder_1_out, multiplexer_1_out;

  Multiplexer #(.width(16)) multiplexer_1 (
    .in0(in_2), .in1(adder_1_out), .out(multiplexer_1_out), .sel(in_3));  // open: en
  or or_1 (or_1_out, in_3, in_4);
  // _16_bit_Register__SR 16_bit_register_sr_1: pin names not known; wires that end beside it: multiplexer_1_out, or_1_out, n16_bit_register_sr_1_p3, out_6
  Adder #(.width(16)) adder_1 (.a(out_6), .b(in_1), .out(adder_1_out));  // open: cin, cout
  Clock clock_1 (.out(n16_bit_register_sr_1_p3));
endmodule

module CPU (
  input  [15:0] DIN,
  input  CLOCK,
  input  INT,
  output MEMLD,
  output [11:0] ADDR,
  output [15:0] DOUT,
  output [15:0] reg0,
  output [15:0] reg1,
  output [15:0] reg2,
  output [15:0] reg3,
  output INTACK,
  output [15:0] reg4,
  output [15:0] reg5,
  output [15:0] reg6,
  output [15:0] reg7
);

  wire IFRST, IFSET, INTLD, IRLD, MUX, PCINCR, PCLD, PCMUX, REGLD, reptile_8_alu_1_zero, SP_minus_minus,
       SP_plus_plus, ZF, ZFLD, ZFPOP;
  wire [1:0] ARMUX, DATAMUX;
  wire [2:0] dst, src1, src2;
  wire [4:0] NEXT_STATE;
  wire [5:0] aluop;
  wire [11:0] adder_1_out, adder_2_out, alu2_12, interrupt_register_1_out_4, ir_1_addr, multiplexer_2_out,
       pc_1_output;
  wire [15:0] mammal_zf_unit_1_to_mem, multiplexer_4_out, multiplexer_5_out,
       n12_16_extender_1_extended_value, reptile_8_alu_1_output;
  wire [15:12] alu2_16;
  wire [24:24] control_unit_1_out_5;

  Multiplexer #(.select(2), .width(12)) multiplexer_1 (
    .in0(pc_1_output), .in1(alu2_12), .in2(reg7[11:0]), .in3(interrupt_register_1_out_4), .out(ADDR),
    .sel(ARMUX));  // open: en
  PC pc_1 (.input_data(multiplexer_2_out), .pc_load(PCLD), .clock(CLOCK), .increment(PCINCR), .\output (pc_1_output));
  Adder #(.width(12)) adder_1 (.a(pc_1_output), .b(ir_1_addr), .out(adder_1_out));  // open: cin, cout
  Multiplexer #(.width(12)) multiplexer_2 (
    .in0(adder_1_out), .in1(DIN[11:0]), .out(multiplexer_2_out), .sel(PCMUX));  // open: en
  Multiplexer #(.select(2), .width(16)) multiplexer_3 (
    .in0(multiplexer_5_out), .in1(n12_16_extender_1_extended_value), .in2(mammal_zf_unit_1_to_mem),
    .out(DOUT), .sel(DATAMUX));  // open: in3, en
  _12_16_extender u_12_16_extender_1 (.Extended_Value(n12_16_extender_1_extended_value), .Input(pc_1_output));
  Interrupt_Register interrupt_register_1 (
    .in_1(adder_2_out), .out_4(interrupt_register_1_out_4), .LD(INTLD), .CLK(CLOCK));
  Adder #(.width(12)) adder_2 (.a(12'h7f0), .b({{9{1'b0}}, DIN[2:0]}), .out(adder_2_out));  // open: cin, cout
  _16_bit_RegBank u_16_bit_regbank_1 (
    .Data_in(multiplexer_4_out), .in_2(REGLD), .reg4(reg4), .reg0(reg0), .reg1(reg1), .reg5(reg5),
    .reg2(reg2), .reg6(reg6), .reg3(reg3), .RegSelect(dst), .CLOCK(CLOCK), .sp_plus(SP_plus_plus),
    .sp_minus(SP_minus_minus), .reg7(reg7));
  mammal_zf_unit mammal_zf_unit_1 (
    .D_0(DIN[0]), .ZF_POP(ZFPOP), .CLOCK(CLOCK), .ZF_LD(ZFLD), .ZF_IN(reptile_8_alu_1_zero),
    .To_mem(mammal_zf_unit_1_to_mem), .ZF(ZF));
  Multiplexer #(.width(16)) multiplexer_4 (
    .in0(reptile_8_alu_1_output), .in1(DIN), .out(multiplexer_4_out), .sel(MUX));  // open: en
  Multiplexer #(.select(3), .width(16)) multiplexer_5 (
    .in0(reg0), .in1(reg1), .in2(reg2), .in3(reg3), .in4(reg4), .in5(reg5), .in6(reg6), .in7(reg7),
    .out(multiplexer_5_out), .sel(src1));  // open: en
  Reptile_8_ALU reptile_8_alu_1 (
    .input1(multiplexer_5_out), .input2({alu2_16, alu2_12}), .\output (reptile_8_alu_1_output),
    .select_bit(aluop), .Zero(reptile_8_alu_1_zero));
  Multiplexer #(.select(3), .width(16)) multiplexer_6 (
    .in0(reg0), .in1(reg1), .in2(reg2), .in3(reg3), .in4(reg4), .in5(reg5), .in6(reg6), .in7(reg7),
    .out({alu2_16, alu2_12}), .sel(src2));  // open: en
  // Probe on reptile_8_alu_1_output
  // Probe on aluop
  // Probe on src1
  // Probe on src2
  IR ir_1 (
    .in_1(DIN[11:0]), .clock(CLOCK), .load(IRLD), .addr(ir_1_addr), .src1(src1), .aluop(aluop), .src2(src2),
    .dst(dst));
  // Probe on dst
  Control_Unit control_unit_1 (
    .opcode(DIN[15:12]), .ZF(ZF),
    .out_5({control_unit_1_out_5[24], DATAMUX, PCMUX, SP_plus_plus, SP_minus_minus, PCLD, PCINCR, ARMUX, REGLD, ZFLD, MUX, MEMLD, IRLD, INTLD, ZFPOP, IFSET, IFRST, INTACK, NEXT_STATE}),
    .INT(INT), .CLK(CLOCK));

  // Other names for the same wires on the sheet: alu2_16[11:0] = alu2_12; R7_12[11:0] = reg7[11:0];
  //   R7_16[15:0] = reg7

  // Notes on the sheet:
  //   *
  //   D-out
endmodule

module _8_bit_Register (
  input  [7:0] in_1,
  input  Load,
  input  Clock,
  output [7:0] Output
);

  wire and_1_out, and_2_out, and_3_out, and_4_out, and_5_out, and_6_out, and_7_out, and_8_out, and_9_out,
       and_10_out, and_11_out, and_12_out, and_13_out, and_14_out, and_15_out, and_16_out;

  and and_1 (and_1_out, in_1[0], Load);
  and and_2 (and_2_out, ~in_1[0], Load);  // AND_Gate
  and and_3 (and_3_out, in_1[1], Load);
  and and_4 (and_4_out, ~in_1[1], Load);  // AND_Gate
  and and_5 (and_5_out, in_1[2], Load);
  and and_6 (and_6_out, ~in_1[2], Load);  // AND_Gate
  and and_7 (and_7_out, in_1[3], Load);
  and and_8 (and_8_out, ~in_1[3], Load);  // AND_Gate
  and and_9 (and_9_out, in_1[4], Load);
  and and_10 (and_10_out, ~in_1[4], Load);  // AND_Gate
  and and_11 (and_11_out, in_1[5], Load);
  and and_12 (and_12_out, ~in_1[5], Load);  // AND_Gate
  and and_13 (and_13_out, in_1[6], Load);
  and and_14 (and_14_out, ~in_1[6], Load);  // AND_Gate
  and and_15 (and_15_out, in_1[7], Load);
  and and_16 (and_16_out, ~in_1[7], Load);  // AND_Gate
  S_R_Flip_Flop s_r_ff_1 (.S(and_1_out), .clk(Clock), .R(and_2_out), .Q(Output[0]));  // open: Qn, preset, reset, en
  S_R_Flip_Flop s_r_ff_2 (.S(and_3_out), .clk(Clock), .R(and_4_out), .Q(Output[1]));  // open: Qn, preset, reset, en
  S_R_Flip_Flop s_r_ff_3 (.S(and_5_out), .clk(Clock), .R(and_6_out), .Q(Output[2]));  // open: Qn, preset, reset, en
  S_R_Flip_Flop s_r_ff_4 (.S(and_7_out), .clk(Clock), .R(and_8_out), .Q(Output[3]));  // open: Qn, preset, reset, en
  S_R_Flip_Flop s_r_ff_5 (.S(and_9_out), .clk(Clock), .R(and_10_out), .Q(Output[4]));  // open: Qn, preset, reset, en
  S_R_Flip_Flop s_r_ff_6 (.S(and_11_out), .clk(Clock), .R(and_12_out), .Q(Output[5]));  // open: Qn, preset, reset, en
  S_R_Flip_Flop s_r_ff_7 (.S(and_13_out), .clk(Clock), .R(and_14_out), .Q(Output[6]));  // open: Qn, preset, reset, en
  S_R_Flip_Flop s_r_ff_8 (.S(and_15_out), .clk(Clock), .R(and_16_out), .Q(Output[7]));  // open: Qn, preset, reset, en
endmodule

module _8_bit_RegBank (
  input  [7:0] Data_in,
  input  [2:0] RegSelect,
  input  Clock,
  output [7:0] out_4,
  output [7:0] out_5,
  output [7:0] out_6,
  output [7:0] out_7,
  output [7:0] out_8,
  output [7:0] out_9,
  output [7:0] out_10,
  output [7:0] out_11
);

  wire and_1_out, and_2_out, and_3_out, and_4_out, and_5_out, and_6_out, and_7_out, and_8_out,
       decoder_1_out0, decoder_1_out1, decoder_1_out2, decoder_1_out3, decoder_1_out4, decoder_1_out5,
       decoder_1_out6, decoder_1_out7, REGLD;

  Decoder #(.select(3), .enable("false")) decoder_1 (
    .out0(decoder_1_out0), .out1(decoder_1_out1), .out2(decoder_1_out2), .out3(decoder_1_out3),
    .out4(decoder_1_out4), .out5(decoder_1_out5), .out6(decoder_1_out6), .out7(decoder_1_out7),
    .sel(RegSelect));
  _8_bit_Register u_8_bit_register_1 (.in_1(Data_in), .Clock(Clock), .Output(out_4), .Load(and_1_out));
  and and_1 (and_1_out, decoder_1_out0, REGLD);
  _8_bit_Register u_8_bit_register_2 (.in_1(Data_in), .Clock(Clock), .Output(out_6), .Load(and_2_out));
  and and_2 (and_2_out, decoder_1_out1, REGLD);
  _8_bit_Register u_8_bit_register_3 (.in_1(Data_in), .Clock(Clock), .Output(out_8), .Load(and_3_out));
  and and_3 (and_3_out, decoder_1_out2, REGLD);
  _8_bit_Register u_8_bit_register_4 (.in_1(Data_in), .Clock(Clock), .Output(out_10), .Load(and_4_out));
  and and_4 (and_4_out, decoder_1_out3, REGLD);
  and and_5 (and_5_out, decoder_1_out4, REGLD);
  and and_6 (and_6_out, decoder_1_out5, REGLD);
  and and_7 (and_7_out, decoder_1_out6, REGLD);
  and and_8 (and_8_out, decoder_1_out7, REGLD);
  _8_bit_Register u_8_bit_register_5 (.in_1(Data_in), .Clock(Clock), .Output(out_5), .Load(and_5_out));
  _8_bit_Register u_8_bit_register_6 (.in_1(Data_in), .Clock(Clock), .Output(out_7), .Load(and_6_out));
  _8_bit_Register u_8_bit_register_7 (.in_1(Data_in), .Clock(Clock), .Output(out_9), .Load(and_7_out));
  _8_bit_Register u_8_bit_register_8 (.in_1(Data_in), .Clock(Clock), .Output(out_11), .Load(and_8_out));
endmodule

module _8_Bit_RegBank_with_MUX (
  input  [7:0] Data_in,
  input  RegLoad_cu,
  input  [2:0] in_3,
  input  [2:0] RegSelect,
  input  [2:0] in_5,
  output [7:0] out_6,
  output [7:0] out_7
);

  wire and_1_out, and_2_out, and_3_out, and_4_out, and_5_out, and_6_out, and_7_out, and_8_out, Clock_out,
       decoder_1_out0, decoder_1_out1, decoder_1_out2, decoder_1_out3, decoder_1_out4, decoder_1_out5,
       decoder_1_out6, decoder_1_out7;
  wire [7:0] n8_bit_register_1_output, n8_bit_register_2_output, n8_bit_register_3_output,
       n8_bit_register_4_output, n8_bit_register_5_output, n8_bit_register_6_output,
       n8_bit_register_7_output, n8_bit_register_8_output;

  Decoder #(.select(3), .enable("false")) decoder_1 (
    .out0(decoder_1_out0), .out1(decoder_1_out1), .out2(decoder_1_out2), .out3(decoder_1_out3),
    .out4(decoder_1_out4), .out5(decoder_1_out5), .out6(decoder_1_out6), .out7(decoder_1_out7),
    .sel(RegSelect));
  Clock Clock (.out(Clock_out));
  _8_bit_Register u_8_bit_register_1 (
    .in_1(Data_in), .Clock(Clock_out), .Output(n8_bit_register_1_output), .Load(and_1_out));
  and and_1 (and_1_out, decoder_1_out0, RegLoad_cu);
  _8_bit_Register u_8_bit_register_2 (
    .in_1(Data_in), .Clock(Clock_out), .Output(n8_bit_register_2_output), .Load(and_2_out));
  and and_2 (and_2_out, decoder_1_out1, RegLoad_cu);
  _8_bit_Register u_8_bit_register_3 (
    .in_1(Data_in), .Clock(Clock_out), .Output(n8_bit_register_3_output), .Load(and_3_out));
  and and_3 (and_3_out, decoder_1_out2, RegLoad_cu);
  _8_bit_Register u_8_bit_register_4 (
    .in_1(Data_in), .Clock(Clock_out), .Output(n8_bit_register_4_output), .Load(and_4_out));
  and and_4 (and_4_out, decoder_1_out3, RegLoad_cu);
  and and_5 (and_5_out, decoder_1_out4, RegLoad_cu);
  and and_6 (and_6_out, decoder_1_out5, RegLoad_cu);
  and and_7 (and_7_out, decoder_1_out6, RegLoad_cu);
  and and_8 (and_8_out, decoder_1_out7, RegLoad_cu);
  _8_bit_Register u_8_bit_register_5 (
    .in_1(Data_in), .Clock(Clock_out), .Output(n8_bit_register_5_output), .Load(and_5_out));
  _8_bit_Register u_8_bit_register_6 (
    .in_1(Data_in), .Clock(Clock_out), .Output(n8_bit_register_6_output), .Load(and_6_out));
  _8_bit_Register u_8_bit_register_7 (
    .in_1(Data_in), .Clock(Clock_out), .Output(n8_bit_register_7_output), .Load(and_7_out));
  _8_bit_Register u_8_bit_register_8 (
    .in_1(Data_in), .Clock(Clock_out), .Output(n8_bit_register_8_output), .Load(and_8_out));
  Multiplexer #(.select(3), .width(8)) multiplexer_1 (
    .in0(n8_bit_register_1_output), .in1(n8_bit_register_2_output), .in2(n8_bit_register_3_output),
    .in3(n8_bit_register_4_output), .in4(n8_bit_register_5_output), .in5(n8_bit_register_6_output),
    .in6(n8_bit_register_7_output), .in7(n8_bit_register_8_output), .out(out_6), .sel(in_3));  // open: en
  Multiplexer #(.select(3), .width(8)) multiplexer_2 (
    .in0(n8_bit_register_1_output), .in1(n8_bit_register_2_output), .in2(n8_bit_register_3_output),
    .in3(n8_bit_register_4_output), .in4(n8_bit_register_5_output), .in5(n8_bit_register_6_output),
    .in6(n8_bit_register_7_output), .out(out_7), .sel(in_5));  // open: in7, en
endmodule

module _7segment_decoder (
  input  A,
  input  B,
  input  C,
  input  D,
  output a_2,
  output b_2,
  output c_2,
  output d_2,
  output e,
  output f,
  output g
);

  wire and_1_out, and_2_out, and_3_out, and_4_out, and_5_out, and_6_out, and_7_out, and_8_out, and_9_out,
       and_10_out, and_11_out, and_12_out, and_13_out, and_14_out, and_15_out, and_16_out, not_1_out,
       not_2_out, not_3_out, not_4_out, not_5_out, not_6_out, not_7_out, not_8_out, not_9_out, not_10_out,
       not_11_out, not_12_out, not_13_out, not_14_out, not_15_out, not_16_out, not_17_out, not_18_out,
       not_19_out, not_20_out, not_21_out;

  not not_1 (not_1_out, B);
  and and_1 (and_1_out, not_1_out, not_2_out);
  not not_2 (not_2_out, D);
  and and_2 (and_2_out, B, D);
  not not_3 (not_3_out, B);
  not not_4 (not_4_out, C);
  and and_3 (and_3_out, not_4_out, not_5_out);
  not not_5 (not_5_out, D);
  and and_4 (and_4_out, C, D);
  not not_6 (not_6_out, C);
  or or_1 (c_2, not_6_out, D, B);
  not not_7 (not_7_out, B);
  and and_5 (and_5_out, not_7_out, not_8_out);
  not not_8 (not_8_out, D);
  not not_9 (not_9_out, B);
  and and_6 (and_6_out, not_9_out, C);
  and and_7 (and_7_out, C, not_10_out);
  not not_10 (not_10_out, D);
  not not_11 (not_11_out, C);
  and and_8 (and_8_out, B, not_11_out, D);
  not not_12 (not_12_out, B);
  and and_9 (and_9_out, not_12_out, not_13_out);
  not not_13 (not_13_out, D);
  and and_10 (and_10_out, C, not_14_out);
  not not_14 (not_14_out, D);
  not not_15 (not_15_out, C);
  and and_11 (and_11_out, not_15_out, not_16_out);
  not not_16 (not_16_out, D);
  and and_12 (and_12_out, B, not_17_out);
  not not_17 (not_17_out, C);
  and and_13 (and_13_out, B, not_18_out);
  not not_18 (not_18_out, D);
  not not_19 (not_19_out, B);
  and and_14 (and_14_out, not_19_out, C);
  and and_15 (and_15_out, B, not_20_out);
  not not_20 (not_20_out, C);
  and and_16 (and_16_out, B, not_21_out);
  not not_21 (not_21_out, D);
  or or_2 (a_2, and_1_out, C, and_2_out, A);
  or or_3 (b_2, not_3_out, and_3_out, and_4_out);
  or or_4 (d_2, and_5_out, and_6_out, and_7_out, and_8_out, A);
  or or_5 (e, and_9_out, and_10_out);
  or or_6 (f, and_11_out, and_12_out, and_13_out, A);
  or or_7 (g, and_14_out, and_15_out, and_16_out, A);
endmodule

module Reptile_8_ALU (
  input  [15:0] input1,
  input  [15:0] input2,
  input  [5:0] select_bit,
  output Zero,
  output [15:0] \output 
);

  wire [15:0] adder_1_out, adder_2_out, and_1_out, multiplexer_1_out, nand_1_out, not_1_out, or_1_out,
       shifter_1_out, subtractor_1_out, subtractor_2_out, xor_1_out;

  Adder #(.width(16)) adder_1 (.a(input1), .b(input2), .out(adder_1_out));  // open: cin, cout
  Subtractor #(.width(16)) subtractor_1 (.a(input1), .b(input2), .out(subtractor_1_out));  // open: bin, bout
  assign and_1_out = input1 & input2;  // AND_Gate and_1, 16 bits wide
  assign or_1_out = input1 | input2;  // OR_Gate or_1, 16 bits wide
  assign xor_1_out = input1 ^ input2;  // XOR_Gate xor_1, 16 bits wide
  Shifter #(.width(16)) shifter_1 (.in(input1), .\dist (input2[3:0]), .out(shifter_1_out));
  assign nand_1_out = ~(input1 & input2);  // NAND_Gate nand_1, 16 bits wide
  assign not_1_out = ~input2;  // NOT_Gate not_1, 16 bits wide
  Multiplexer #(.select(3), .width(16)) multiplexer_1 (
    .in0(not_1_out), .in1(input2), .in2(adder_2_out), .in3(subtractor_2_out), .out(multiplexer_1_out),
    .sel({1'b0, select_bit[1:0]}));  // open: in4, in5, in6, in7, en
  Adder #(.width(16)) adder_2 (.a(input2), .b(16'h1), .out(adder_2_out));  // open: cin, cout
  Subtractor #(.width(16)) subtractor_2 (.a(input2), .b(16'h1), .out(subtractor_2_out));  // open: bin, bout
  Multiplexer #(.select(3), .width(16)) multiplexer_2 (
    .in0(adder_1_out), .in1(subtractor_1_out), .in2(and_1_out), .in3(or_1_out), .in4(xor_1_out),
    .in5(shifter_1_out), .in6(nand_1_out), .in7(multiplexer_1_out), .out(\output ), .sel(select_bit[5:3]));  // open: en
  nor nor_1 (Zero, \output [0], \output [1], \output [2], \output [3], \output [4], \output [5], \output [6], \output [7], \output [9], \output [10], \output [11], \output [12], \output [13], \output [14], \output [15], \output [8]);

  // Notes on the sheet:
  //   ADDER
  //   SUBTRACTOR
  //   AND
  //   OR
endmodule

module increment (
  input  [15:0] \input ,
  output [15:0] \output 
);

  Adder #(.width(16)) adder_1 (.a(\input ), .b(16'h1), .out(\output ));  // open: cin, cout
endmodule

module Decrement (
  input  [15:0] \input ,
  output [15:0] \output 
);

  Subtractor #(.width(16)) subtractor_1 (.a(\input ), .b(16'h1), .out(\output ));  // open: bin, bout
endmodule

module ZF_Unit (
  input  Data,
  input  Load,
  input  clk,
  output Output
);

  wire and_1_out, and_2_out, not_1_out;

  not not_1 (not_1_out, Data);
  and and_1 (and_1_out, Data, Load);
  and and_2 (and_2_out, not_1_out, Load);
  S_R_Flip_Flop s_r_ff_1 (.S(and_1_out), .clk(clk), .R(and_2_out), .Q(Output));  // open: Qn, preset, reset, en
endmodule

module IR (
  input  [11:0] in_1,
  input  clock,
  input  load,
  output [11:0] addr,
  output [2:0] dst,
  output [2:0] src1,
  output [2:0] src2,
  output [5:0] aluop
);

  _12_bit_register u_12_bit_register_1 (.in_1(in_1), .Clock(clock), .Output(addr), .Load(load));

  assign aluop = addr[11:6];
  assign dst = addr[2:0];
  assign src1 = addr[8:6];
  assign src2 = addr[5:3];
endmodule

module _12_bit_register (
  input  [11:0] in_1,
  input  Load,
  input  Clock,
  output [11:0] Output
);

  wire and_1_out, and_2_out, and_3_out, and_4_out, and_5_out, and_6_out, and_7_out, and_8_out, and_9_out,
       and_10_out, and_11_out, and_12_out, and_13_out, and_14_out, and_15_out, and_16_out, and_17_out,
       and_18_out, and_19_out, and_20_out, and_21_out, and_22_out, and_23_out, and_24_out;

  and and_1 (and_1_out, in_1[0], Load);
  and and_2 (and_2_out, ~in_1[0], Load);  // AND_Gate
  and and_3 (and_3_out, in_1[1], Load);
  and and_4 (and_4_out, ~in_1[1], Load);  // AND_Gate
  and and_5 (and_5_out, in_1[2], Load);
  and and_6 (and_6_out, ~in_1[2], Load);  // AND_Gate
  and and_7 (and_7_out, in_1[3], Load);
  and and_8 (and_8_out, ~in_1[3], Load);  // AND_Gate
  and and_9 (and_9_out, in_1[4], Load);
  and and_10 (and_10_out, ~in_1[4], Load);  // AND_Gate
  and and_11 (and_11_out, in_1[5], Load);
  and and_12 (and_12_out, ~in_1[5], Load);  // AND_Gate
  and and_13 (and_13_out, in_1[6], Load);
  and and_14 (and_14_out, ~in_1[6], Load);  // AND_Gate
  and and_15 (and_15_out, in_1[7], Load);
  and and_16 (and_16_out, ~in_1[7], Load);  // AND_Gate
  and and_17 (and_17_out, in_1[8], Load);
  and and_18 (and_18_out, ~in_1[8], Load);  // AND_Gate
  and and_19 (and_19_out, in_1[9], Load);
  and and_20 (and_20_out, ~in_1[9], Load);  // AND_Gate
  and and_21 (and_21_out, in_1[10], Load);
  and and_22 (and_22_out, ~in_1[10], Load);  // AND_Gate
  and and_23 (and_23_out, in_1[11], Load);
  and and_24 (and_24_out, ~in_1[11], Load);  // AND_Gate
  S_R_Flip_Flop s_r_ff_1 (.S(and_1_out), .clk(Clock), .R(and_2_out), .Q(Output[0]));  // open: Qn, preset, reset, en
  S_R_Flip_Flop s_r_ff_2 (.S(and_3_out), .clk(Clock), .R(and_4_out), .Q(Output[1]));  // open: Qn, preset, reset, en
  S_R_Flip_Flop s_r_ff_3 (.S(and_5_out), .clk(Clock), .R(and_6_out), .Q(Output[2]));  // open: Qn, preset, reset, en
  S_R_Flip_Flop s_r_ff_4 (.S(and_7_out), .clk(Clock), .R(and_8_out), .Q(Output[3]));  // open: Qn, preset, reset, en
  S_R_Flip_Flop s_r_ff_5 (.S(and_9_out), .clk(Clock), .R(and_10_out), .Q(Output[4]));  // open: Qn, preset, reset, en
  S_R_Flip_Flop s_r_ff_6 (.S(and_11_out), .clk(Clock), .R(and_12_out), .Q(Output[5]));  // open: Qn, preset, reset, en
  S_R_Flip_Flop s_r_ff_7 (.S(and_13_out), .clk(Clock), .R(and_14_out), .Q(Output[6]));  // open: Qn, preset, reset, en
  S_R_Flip_Flop s_r_ff_8 (.S(and_15_out), .clk(Clock), .R(and_16_out), .Q(Output[7]));  // open: Qn, preset, reset, en
  S_R_Flip_Flop s_r_ff_9 (.S(and_17_out), .clk(Clock), .R(and_18_out), .Q(Output[8]));  // open: Qn, preset, reset, en
  S_R_Flip_Flop s_r_ff_10 (.S(and_19_out), .clk(Clock), .R(and_20_out), .Q(Output[9]));  // open: Qn, preset, reset, en
  S_R_Flip_Flop s_r_ff_11 (.S(and_21_out), .clk(Clock), .R(and_22_out), .Q(Output[10]));  // open: Qn, preset, reset, en
  S_R_Flip_Flop s_r_ff_12 (.S(and_23_out), .clk(Clock), .R(and_24_out), .Q(Output[11]));  // open: Qn, preset, reset, en
endmodule

module _16_bit_RegBank (
  input  [15:0] Data_in,
  input  in_2,
  input  [2:0] RegSelect,
  input  sp_minus,
  input  sp_plus,
  input  CLOCK,
  output [15:0] reg0,
  output [15:0] reg4,
  output [15:0] reg1,
  output [15:0] reg5,
  output [15:0] reg2,
  output [15:0] reg6,
  output [15:0] reg7,
  output [15:0] reg3
);

  wire and_1_out, and_2_out, and_3_out, and_4_out, and_5_out, and_6_out, and_7_out, and_8_out,
       decoder_1_out0, decoder_1_out1, decoder_1_out2, decoder_1_out3, decoder_1_out4, decoder_1_out5,
       decoder_1_out6, decoder_1_out7;
  wire [15:0] adder_1_out, multiplexer_1_out, subtractor_1_out;

  Decoder #(.select(3), .enable("false")) decoder_1 (
    .out0(decoder_1_out0), .out1(decoder_1_out1), .out2(decoder_1_out2), .out3(decoder_1_out3),
    .out4(decoder_1_out4), .out5(decoder_1_out5), .out6(decoder_1_out6), .out7(decoder_1_out7),
    .sel(RegSelect));
  _16_bit_Register__SR u_16_bit_register_sr_1 (.Output(reg0), .Load(and_1_out), .in_1(Data_in), .Clock(CLOCK));
  and and_1 (and_1_out, decoder_1_out0, in_2);
  _16_bit_Register__SR u_16_bit_register_sr_2 (.Output(reg1), .Load(and_2_out), .in_1(Data_in), .Clock(CLOCK));
  and and_2 (and_2_out, decoder_1_out1, in_2);
  _16_bit_Register__SR u_16_bit_register_sr_3 (.Output(reg2), .Load(and_3_out), .in_1(Data_in), .Clock(CLOCK));
  and and_3 (and_3_out, decoder_1_out2, in_2);
  _16_bit_Register__SR u_16_bit_register_sr_4 (.Output(reg3), .Load(and_4_out), .in_1(Data_in), .Clock(CLOCK));
  and and_4 (and_4_out, decoder_1_out3, in_2);
  and and_5 (and_5_out, decoder_1_out4, in_2);
  and and_6 (and_6_out, decoder_1_out5, in_2);
  and and_7 (and_7_out, decoder_1_out6, in_2);
  _16_bit_Register__SR u_16_bit_register_sr_5 (.Output(reg4), .Load(and_5_out), .in_1(Data_in), .Clock(CLOCK));
  _16_bit_Register__SR u_16_bit_register_sr_6 (.Output(reg5), .Load(and_6_out), .in_1(Data_in), .Clock(CLOCK));
  _16_bit_Register__SR u_16_bit_register_sr_7 (.Output(reg6), .Load(and_7_out), .in_1(Data_in), .Clock(CLOCK));
  and and_8 (and_8_out, decoder_1_out7, in_2);
  _16_bit_Register__SR u_16_bit_register_sr_8 (
    .Output(reg7), .Load(and_8_out), .in_1(multiplexer_1_out), .Clock(CLOCK));
  Adder #(.width(16)) adder_1 (.a(reg7), .b(16'h1), .out(adder_1_out));  // open: cin, cout
  Subtractor #(.width(16)) subtractor_1 (.a(reg7), .b(16'h1), .out(subtractor_1_out));  // open: bin, bout
  Multiplexer #(.select(2), .width(16)) multiplexer_1 (
    .in0(Data_in), .in1(adder_1_out), .in2(subtractor_1_out), .in3(subtractor_1_out),
    .out(multiplexer_1_out), .sel({sp_minus, sp_plus}));  // open: en
endmodule

module PC (
  input  [11:0] input_data,
  input  pc_load,
  input  clock,
  input  increment,
  output [11:0] \output 
);

  wire or_1_out;
  wire [11:0] adder_1_out, multiplexer_1_out;

  or or_1 (or_1_out, pc_load, increment);
  _12_bit_register u_12_bit_register_1 (.in_1(multiplexer_1_out), .Clock(clock), .Output(\output ), .Load(or_1_out));
  Adder #(.width(12)) adder_1 (.a(\output ), .b(12'h1), .out(adder_1_out));  // open: cin, cout
  Multiplexer #(.width(12), .enable("false")) multiplexer_1 (
    .in0(input_data), .in1(adder_1_out), .out(multiplexer_1_out), .sel(increment));
endmodule

module Control_Unit (
  input  [3:0] opcode,
  input  CLK,
  input  INT,
  input  ZF,
  output [24:0] out_5
);

  wire and_2_out, and_3_out, not_1_out, not_2_out, not_3_out, s_r_ff_1_q;
  wire [1:1] and_1_out;
  wire [3:0] multiplexer_2_out;
  wire [4:0] multiplexer_1_out, multiplexer_3_out, n5_bit_register_1_output;

  and and_1 (and_1_out[1], not_1_out, not_2_out, opcode[2], not_3_out);
  not not_1 (not_1_out, opcode[0]);
  not not_2 (not_2_out, opcode[1]);
  not not_3 (not_3_out, opcode[3]);
  Multiplexer #(.width(5)) multiplexer_1 (
    .in0(out_5[4:0]), .in1({1'b0, multiplexer_2_out}), .out(multiplexer_1_out), .sel(out_5[24]));  // open: en
  Multiplexer #(.select(2), .width(4), .enable("false")) multiplexer_2 (
    .in0(opcode), .in1(opcode), .in2(4'b0000), .in3(4'b0101), .out(multiplexer_2_out),
    .sel({and_1_out[1], ZF}));
  Multiplexer #(.width(5)) multiplexer_3 (
    .in0(multiplexer_1_out), .in1(5'b10011), .out(multiplexer_3_out), .sel(and_2_out));  // open: en
  _5_bit_register u_5_bit_register_1 (
    .in_1(multiplexer_3_out), .Clock(CLK), .Output(n5_bit_register_1_output), .Load(1'b1));
  ROM #(.addrWidth(5), .dataWidth(25)) rom_1 (.addr(n5_bit_register_1_output), .data(out_5));  // open: sel
  and and_2 (and_2_out, INT, s_r_ff_1_q, and_3_out);
  and and_3 (and_3_out, ~out_5[4], ~out_5[3], ~out_5[2], ~out_5[1], ~out_5[0]);  // AND_Gate
  S_R_Flip_Flop s_r_ff_1 (.S(out_5[7]), .clk(CLK), .R(out_5[6]), .Q(s_r_ff_1_q));  // open: Qn, preset, reset, en

  // Other names for the same wires on the sheet: ARMUX[1:0] = out_5[16:15]; NEXT_STATE[4:0] = out_5[4:0];
  //   INTACK = out_5[5]; IFRST = out_5[6]; IFSET = out_5[7]; ZFPOP = out_5[8]; INTLD = out_5[9]; IRLD = out_5[10];
  //   MEMLD = out_5[11]; MUX = out_5[12]; ZFLD = out_5[13]; REGLD = out_5[14]; PCINC = out_5[17]; PCLD = out_5[18];
  //   SP_minus_minus = out_5[19]; SP_plus_plus = out_5[20]; PCMUX = out_5[21]; DATAMUX[1:0] = out_5[23:22]

  // Notes on the sheet:
  //   ISR ADRESS OF INT1
  //   contents of rom_1 (hex, n*v repeats v):
  //   102041f 25000 d000 8800 0 40000 0 6000 90000 100011 550800 100012 80 40 10000f 111110 250000 15000
  //   251000 490854 890a35 258000
endmodule

module PLAYGROUND (
  input  [7:0] CLOCK,
  input  [2:0] CLOCK_2,
  output [7:0] MEMLD
);

  wire CLOCK_t, cpu_1_intack, MEMLD_t, pic_1_interrupt, timer_1_p2;
  wire [11:0] ADDR;
  wire [15:0] DEVICEID, DIN, DOUT, TIME;

  // Timer timer_1: pin names not known; wires that end beside it: TIME, timer_1_p2
  Shifter shifter_1 (.in(CLOCK), .\dist (CLOCK_2), .out(MEMLD));
  PIC pic_1 (
    .\devıce0 (timer_1_p2), .out_11(DEVICEID), .INTERRUPT(pic_1_interrupt), .CLK(CLOCK_t),
    .INTACK(cpu_1_intack));  // open: device1, device2, device3, device4, device5, device6, device7
  CPU cpu_1 (
    .INT(pic_1_interrupt), .ADDR(ADDR), .INTACK(cpu_1_intack), .MEMLD(MEMLD_t), .DOUT(DOUT), .DIN(DIN),
    .CLOCK(CLOCK_t));  // open: reg0, reg1, reg2, reg3, reg4, reg5, reg6, reg7
  RAM #(.bus("separate")) ram_1 ();  // open: addr, din, data, str, sel, clk, ld, clr
endmodule

module _4_bit_register (
  input  [3:0] in_1,
  input  Clock,
  output [15:0] _16b_out,
  output [3:0] Output
);

  wire and_1_out, and_2_out, and_3_out, and_4_out, and_5_out, and_6_out, and_7_out, and_8_out;

  and and_1 (and_1_out, in_1[0], 1'b1);
  and and_2 (and_2_out, ~in_1[0], 1'b1);  // AND_Gate
  and and_3 (and_3_out, in_1[1], 1'b1);
  and and_4 (and_4_out, ~in_1[1], 1'b1);  // AND_Gate
  and and_5 (and_5_out, in_1[2], 1'b1);
  and and_6 (and_6_out, ~in_1[2], 1'b1);  // AND_Gate
  and and_7 (and_7_out, in_1[3], 1'b1);
  and and_8 (and_8_out, ~in_1[3], 1'b1);  // AND_Gate
  S_R_Flip_Flop s_r_ff_1 (.S(and_1_out), .clk(Clock), .R(and_2_out), .Q(Output[0]));  // open: Qn, preset, reset, en
  S_R_Flip_Flop s_r_ff_2 (.S(and_3_out), .clk(Clock), .R(and_4_out), .Q(Output[1]));  // open: Qn, preset, reset, en
  S_R_Flip_Flop s_r_ff_3 (.S(and_5_out), .clk(Clock), .R(and_6_out), .Q(Output[2]));  // open: Qn, preset, reset, en
  S_R_Flip_Flop s_r_ff_4 (.S(and_7_out), .clk(Clock), .R(and_8_out), .Q(Output[3]));  // open: Qn, preset, reset, en
  assign _16b_out = {{12{1'b0}}, Output};  // Bit_Extender bit_extender_1
endmodule

module _7th_Register_Stack (
  input  [15:0] in_1,
  input  CLOCK,
  input  LD,
  input  sp_plus_plus,
  input  sp_minus_minus,
  output [15:0] OUTPUT
);

  wire or_1_out, or_2_out;
  wire [15:0] adder_1_out, DATA, multiplexer_1_out, subtractor_1_out;

  Multiplexer #(.width(16), .enable("false")) multiplexer_1 (
    .in0(in_1), .in1(DATA), .out(multiplexer_1_out), .sel(or_1_out));
  or or_1 (or_1_out, sp_plus_plus, sp_minus_minus);
  or or_2 (or_2_out, sp_plus_plus, sp_minus_minus, LD);
  _16_bit_Register__SR u_16_bit_register_sr_1 (
    .Output(OUTPUT), .Load(or_2_out), .in_1(multiplexer_1_out), .Clock(CLOCK));
  Adder #(.width(16)) adder_1 (.a(OUTPUT), .b(16'h1), .out(adder_1_out));  // open: cin, cout
  Subtractor #(.width(16)) subtractor_1 (.a(OUTPUT), .b(16'h1), .out(subtractor_1_out));  // open: bin, bout
  Multiplexer #(.width(16), .enable("false")) multiplexer_2 (
    .in0(adder_1_out), .in1(subtractor_1_out), .out(DATA), .sel(sp_minus_minus));
endmodule

module mammal_zf_unit (
  input  D_0,
  input  ZF_POP,
  input  CLOCK,
  input  ZF_LD,
  input  ZF_IN,
  output [15:0] To_mem,
  output ZF
);

  wire and_1_out, and_2_out, and_3_out, and_4_out, or_1_out, or_2_out;

  and and_1 (and_1_out, D_0, ZF_POP);
  and and_2 (and_2_out, ZF_POP, ~D_0);  // AND_Gate
  and and_3 (and_3_out, ZF_LD, ZF_IN);
  and and_4 (and_4_out, ~ZF_IN, ZF_LD);  // AND_Gate
  or or_1 (or_1_out, and_1_out, and_3_out);
  or or_2 (or_2_out, and_2_out, and_4_out);
  S_R_Flip_Flop s_r_ff_1 (.S(or_1_out), .clk(CLOCK), .R(or_2_out), .Q(ZF));  // open: Qn, preset, reset, en
  assign To_mem = {{15{1'b0}}, ZF};  // Bit_Extender bit_extender_1
endmodule

module Interrupt_Register (
  input  [11:0] in_1,
  input  LD,
  input  CLK,
  output [11:0] out_4
);

  _4_bit_register_with_manuel_load u_4_bit_register_with_manuel_load_1 (
    .in_1(in_1[3:0]), .Clock(CLK), .Output(out_4[3:0]), .LD(LD));
  _4_bit_register_with_manuel_load u_4_bit_register_with_manuel_load_2 (
    .in_1(in_1[7:4]), .Clock(CLK), .Output(out_4[7:4]), .LD(LD));
  _4_bit_register_with_manuel_load u_4_bit_register_with_manuel_load_3 (
    .in_1(in_1[11:8]), .Clock(CLK), .Output(out_4[11:8]), .LD(LD));
endmodule

module _4_bit_register_with_manuel_load (
  input  [3:0] in_1,
  input  LD,
  input  Clock,
  output [3:0] Output
);

  wire and_1_out, and_2_out, and_3_out, and_4_out, and_5_out, and_6_out, and_7_out, and_8_out;

  and and_1 (and_1_out, in_1[0], LD);
  and and_2 (and_2_out, ~in_1[0], LD);  // AND_Gate
  and and_3 (and_3_out, in_1[1], LD);
  and and_4 (and_4_out, ~in_1[1], LD);  // AND_Gate
  and and_5 (and_5_out, in_1[2], LD);
  and and_6 (and_6_out, ~in_1[2], LD);  // AND_Gate
  and and_7 (and_7_out, in_1[3], LD);
  and and_8 (and_8_out, ~in_1[3], LD);  // AND_Gate
  S_R_Flip_Flop s_r_ff_1 (.S(and_1_out), .clk(Clock), .R(and_2_out), .Q(Output[0]));  // open: Qn, preset, reset, en
  S_R_Flip_Flop s_r_ff_2 (.S(and_3_out), .clk(Clock), .R(and_4_out), .Q(Output[1]));  // open: Qn, preset, reset, en
  S_R_Flip_Flop s_r_ff_3 (.S(and_5_out), .clk(Clock), .R(and_6_out), .Q(Output[2]));  // open: Qn, preset, reset, en
  S_R_Flip_Flop s_r_ff_4 (.S(and_7_out), .clk(Clock), .R(and_8_out), .Q(Output[3]));  // open: Qn, preset, reset, en
endmodule

module _5_bit_register (
  input  [4:0] in_1,
  input  Load,
  input  Clock,
  output [4:0] Output
);

  wire and_1_out, and_2_out, and_3_out, and_4_out, and_5_out, and_6_out, and_7_out, and_8_out, and_9_out,
       and_10_out;

  and and_1 (and_1_out, in_1[0], Load);
  and and_2 (and_2_out, ~in_1[0], Load);  // AND_Gate
  and and_3 (and_3_out, in_1[1], Load);
  and and_4 (and_4_out, ~in_1[1], Load);  // AND_Gate
  and and_5 (and_5_out, in_1[2], Load);
  and and_6 (and_6_out, ~in_1[2], Load);  // AND_Gate
  and and_7 (and_7_out, in_1[3], Load);
  and and_8 (and_8_out, ~in_1[3], Load);  // AND_Gate
  and and_9 (and_9_out, in_1[4], Load);
  and and_10 (and_10_out, ~in_1[4], Load);  // AND_Gate
  S_R_Flip_Flop s_r_ff_1 (.S(and_1_out), .clk(Clock), .R(and_2_out), .Q(Output[0]));  // open: Qn, preset, reset, en
  S_R_Flip_Flop s_r_ff_2 (.S(and_3_out), .clk(Clock), .R(and_4_out), .Q(Output[1]));  // open: Qn, preset, reset, en
  S_R_Flip_Flop s_r_ff_3 (.S(and_5_out), .clk(Clock), .R(and_6_out), .Q(Output[2]));  // open: Qn, preset, reset, en
  S_R_Flip_Flop s_r_ff_4 (.S(and_7_out), .clk(Clock), .R(and_8_out), .Q(Output[3]));  // open: Qn, preset, reset, en
  S_R_Flip_Flop s_r_ff_5 (.S(and_9_out), .clk(Clock), .R(and_10_out), .Q(Output[4]));  // open: Qn, preset, reset, en
endmodule

module Timer (
  input  CLK,
  output INTERRUPT,
  output [15:0] out_3
);

  wire [15:0] adder_1_out, adder_2_out, multiplexer_1_out, n16_bit_register_sr_1_output;

  _16_bit_Register__SR u_16_bit_register_sr_1 (
    .Output({n16_bit_register_sr_1_output[15:10], INTERRUPT, n16_bit_register_sr_1_output[8:0]}),
    .Load(1'b1), .in_1(multiplexer_1_out), .Clock(CLK));
  Multiplexer #(.width(16)) multiplexer_1 (
    .in0(adder_1_out), .in1({16{1'b0}}), .out(multiplexer_1_out), .sel(INTERRUPT));  // open: en
  Adder #(.width(16)) adder_1 (
    .a(16'h1), .b({n16_bit_register_sr_1_output[15:10], INTERRUPT, n16_bit_register_sr_1_output[8:0]}),
    .out(adder_1_out));  // open: cin, cout
  _16_bit_Register__SR u_16_bit_register_sr_2 (.Output(out_3), .Load(INTERRUPT), .in_1(adder_2_out), .Clock(CLK));
  Adder #(.width(16)) adder_2 (.a(16'h1), .b(out_3), .out(adder_2_out));  // open: cin, cout
endmodule

module PIC (
  input  CLK,
  input  \devıce0 ,
  input  device1,
  input  device2,
  input  device3,
  input  device4,
  input  device5,
  input  device6,
  input  INTACK,
  input  device7,
  output [15:0] out_11,
  output INTERRUPT
);

  wire priority_encoder_1_gs;
  wire [2:0] priority_encoder_1_out, register_1_q;

  Priority_Encoder #(.disabled(0)) priority_encoder_1 (
    .in0(\devıce0 ), .in1(device1), .in2(device2), .in3(device3), .in4(device4), .in5(device5),
    .in6(device6), .in7(device7), .out(priority_encoder_1_out), .gs(priority_encoder_1_gs));  // open: en_in, en_out
  Register #(.width(3)) register_1 (.D(priority_encoder_1_out), .Q(register_1_q), .clk(CLK));  // open: en, clr
  S_R_Flip_Flop s_r_ff_1 (
    .S(priority_encoder_1_gs), .clk(CLK), .R(INTACK), .Q(INTERRUPT));  // open: Qn, preset, reset, en
  assign out_11 = {{13{1'b0}}, register_1_q};  // Bit_Extender bit_extender_1
endmodule

module MAIN (
  input  [3:0] INPUT,
  input  in_2,
  output [15:0] d,
  output [15:0] d_2,
  output [15:0] d_3,
  output [15:0] d_4,
  output [15:0] d_5,
  output [15:0] d_6,
  output [15:0] d_7,
  output [15:0] d_8
);

  wire and_1_out, and_2_out, BTN_out, CLOCK, comparator_1_eq, comparator_1_gt, comparator_1_lt,
       comparator_2_eq, comparator_3_eq, comparator_4_eq, comparator_5_eq, comparator_6_eq, INTACK, MEMLD,
       n1bit_register_1_out, or_1_out, pic_1_interrupt, timer_1_interrupt;
  wire [3:0] doubledabble_1_hundreds, doubledabble_1_tens, doubledabble_1_thosands, doubledabble_1_unit;
  wire [11:0] ADDR, multiplexer_1_out;
  wire [15:0] _7SEG, BUTTON, \DEVİCEID , DIN, DOUT, INPUT_t, multiplexer_2_out, multiplexer_3_out,
       multiplexer_4_out, multiplexer_5_out, ram_1_data, SWITCH, TIME;

  Comparator #(.width(12)) comparator_1 (
    .a(ADDR), .b(12'ha06), .gt(comparator_1_gt), .eq(comparator_1_eq), .lt(comparator_1_lt));
  Button_part BTN (.out(BTN_out));
  // Probe on BTN_out
  Clock clock_1 (.out(CLOCK));
  Multiplexer #(.width(12), .enable("false")) multiplexer_1 (
    .in0({12{1'b0}}), .in1(ADDR), .out(multiplexer_1_out), .sel(n1bit_register_1_out));
  // Probe on ADDR
  or or_1 (or_1_out, comparator_1_gt, comparator_1_lt);
  _1bit_register u_1bit_register_1 (.DATA(1'b1), .CLK(CLOCK), .LOAD(1'b1), .OUT(n1bit_register_1_out));
  and and_1 (and_1_out, MEMLD, or_1_out);
  and and_2 (and_2_out, comparator_1_eq, MEMLD);
  Comparator #(.width(12)) comparator_2 (.a(12'ha04), .b(ADDR), .eq(comparator_2_eq));  // open: gt, lt
  Hex_Digit_Display hex_digit_display_1 (.value(doubledabble_1_hundreds));  // open: dp
  Hex_Digit_Display hex_digit_display_2 (.value(doubledabble_1_thosands));  // open: dp
  _16_bit_Register__SR u_16_bit_register_sr_1 (.Output(_7SEG), .Load(and_2_out), .in_1(DOUT), .Clock(CLOCK));
  Button button_1 (.CLOCK(CLOCK), .OUT(BUTTON), .IN(BTN_out), .RESET(comparator_2_eq));
  // Probe on BUTTON
  _4_bit_register u_4_bit_register_1 (.in_1(INPUT), .Clock(CLOCK), ._16b_out(INPUT_t));  // open: Output
  Hex_Digit_Display hex_digit_display_3 (.value(doubledabble_1_tens));  // open: dp
  Hex_Digit_Display hex_digit_display_4 (.value(doubledabble_1_unit));  // open: dp
  doubledabble doubledabble_1 (
    .unit(doubledabble_1_unit), .tens(doubledabble_1_tens), .hundreds(doubledabble_1_hundreds),
    .thosands(doubledabble_1_thosands), .in_1(_7SEG));
  Timer timer_1 (.out_3(TIME), .INTERRUPT(timer_1_interrupt), .CLK(CLOCK));
  PIC pic_1 (
    .\devıce0 (timer_1_interrupt), .out_11(\DEVİCEID ), .INTERRUPT(pic_1_interrupt), .CLK(CLOCK),
    .INTACK(INTACK));  // open: device1, device2, device3, device4, device5, device6, device7
  RAM #(.addrWidth(12), .dataWidth(16), .bus("separate")) ram_1 (
    .addr(multiplexer_1_out), .din(DOUT), .data(ram_1_data), .str(and_1_out), .clk(CLOCK));  // open: sel, ld, clr
  assign SWITCH = {{15{1'b0}}, in_2};  // Bit_Extender bit_extender_1
  CPU cpu_1 (
    .INT(pic_1_interrupt), .ADDR(ADDR), .INTACK(INTACK), .MEMLD(MEMLD), .DOUT(DOUT), .DIN(DIN),
    .CLOCK(CLOCK), .reg0(d), .reg1(d_2), .reg2(d_3), .reg3(d_4), .reg4(d_5), .reg5(d_6), .reg6(d_7),
    .reg7(d_8));
  Comparator #(.width(12)) comparator_3 (.a(12'ha00), .b(ADDR), .eq(comparator_3_eq));  // open: gt, lt
  Multiplexer #(.width(16), .enable("false")) multiplexer_2 (
    .in0(ram_1_data), .in1(TIME), .out(multiplexer_2_out), .sel(comparator_3_eq));
  Comparator #(.width(12)) comparator_4 (.a(12'ha02), .b(ADDR), .eq(comparator_4_eq));  // open: gt, lt
  Multiplexer #(.width(16), .enable("false")) multiplexer_3 (
    .in0(multiplexer_2_out), .in1(INPUT_t), .out(multiplexer_3_out), .sel(comparator_4_eq));
  Comparator #(.width(12)) comparator_5 (.a(12'ha04), .b(ADDR), .eq(comparator_5_eq));  // open: gt, lt
  Multiplexer #(.width(16), .enable("false")) multiplexer_4 (
    .in0(multiplexer_3_out), .in1(BUTTON), .out(multiplexer_4_out), .sel(comparator_5_eq));
  Comparator #(.width(12)) comparator_6 (.a(12'ha08), .b(ADDR), .eq(comparator_6_eq));  // open: gt, lt
  // Probe on DIN
  Multiplexer #(.width(16), .enable("false")) multiplexer_5 (
    .in0(multiplexer_4_out), .in1(SWITCH), .out(multiplexer_5_out), .sel(comparator_6_eq));
  Multiplexer #(.width(16), .enable("false")) multiplexer_6 (
    .in0(multiplexer_5_out), .in1(\DEVİCEID ), .out(DIN), .sel(INTACK));

  // Notes on the sheet:
  //   a06 olacak
endmodule

module Button (
  input  CLOCK,
  input  IN,
  input  RESET,
  output [15:0] OUT
);

  wire and_1_out, and_2_out, and_3_out, not_1_out, not_2_out, s_r_ff_1_q, s_r_ff_2_q, s_r_ff_3_q;

  not not_1 (not_1_out, IN);
  S_R_Flip_Flop s_r_ff_1 (.S(IN), .clk(CLOCK), .R(not_1_out), .Q(s_r_ff_1_q));  // open: Qn, preset, reset, en
  S_R_Flip_Flop s_r_ff_2 (.S(s_r_ff_1_q), .clk(CLOCK), .R(not_2_out), .Q(s_r_ff_2_q));  // open: Qn, preset, reset, en
  not not_2 (not_2_out, s_r_ff_1_q);
  and and_1 (and_1_out, s_r_ff_1_q, ~s_r_ff_2_q);  // AND_Gate
  and and_2 (and_2_out, ~s_r_ff_3_q, and_1_out);  // AND_Gate
  and and_3 (and_3_out, RESET, s_r_ff_3_q);
  S_R_Flip_Flop s_r_ff_3 (.S(and_2_out), .clk(CLOCK), .R(and_3_out), .Q(s_r_ff_3_q));  // open: Qn, preset, reset, en
  assign OUT = {{15{1'b0}}, s_r_ff_3_q};  // Bit_Extender bit_extender_1
endmodule

module _1bit_register (
  input  DATA,
  input  CLK,
  input  LOAD,
  output OUT
);

  wire and_1_out, and_2_out, not_1_out;

  not not_1 (not_1_out, DATA);
  and and_1 (and_1_out, DATA, LOAD);
  and and_2 (and_2_out, not_1_out, LOAD);
  S_R_Flip_Flop s_r_ff_1 (.S(and_1_out), .clk(CLK), .R(and_2_out), .Q(OUT));  // open: Qn, preset, reset, en
endmodule

module _12_16_extender (
  input  [11:0] Input,
  output [15:0] Extended_Value
);


  assign Extended_Value = {Input, 4'b0000};
endmodule

module jlokjkljk (
  input  [15:0] INPUT_2,
  input  [15:0] INPUT_1,
  input  in_3,
  input  [15:0] in_4,
  output [15:0] out_5,
  output [15:0] out_6,
  output [15:0] out_7,
  output [15:0] out_8,
  output [15:0] out_9,
  output [15:0] out_10,
  output [15:0] out_11,
  output [15:0] out_12
);

  wire and_1_out, and_2_out, BUTTON_1_out, BUTTON_2_out, CLOCK, comparator_1_eq, comparator_2_eq,
       comparator_3_eq, comparator_3_gt, comparator_3_lt, comparator_4_eq, comparator_5_eq, comparator_6_eq,
       comparator_7_eq, comparator_8_eq, comparator_9_eq, INT_ACK, MEMWT, n1bit_register_1_out, or_1_out,
       pic_1_interrupt, timer_1_interrupt;
  wire [11:0] ADDR, multiplexer_1_out;
  wire [15:0] _7SEG_OUT, BUTTON_1, BUTTON_2, DIN, DOUT, INPUT_1_t, INPUT_2_t, INT_DEVICE_ID,
       multiplexer_2_out, multiplexer_3_out, multiplexer_4_out, multiplexer_5_out, multiplexer_6_out,
       multiplexer_7_out, ram_1_data, SWITCH, TIME;

  Clock clock_1 (.out(CLOCK));
  PIC pic_1 (
    .\devıce0 (timer_1_interrupt), .out_11(INT_DEVICE_ID), .INTERRUPT(pic_1_interrupt), .CLK(CLOCK),
    .INTACK(INT_ACK));  // open: device1, device2, device3, device4, device5, device6, device7
  Timer timer_1 (.out_3(TIME), .INTERRUPT(timer_1_interrupt), .CLK(CLOCK));
  assign SWITCH = {{15{1'b0}}, in_3};  // Bit_Extender bit_extender_1
  CPU cpu_1 (
    .INT(pic_1_interrupt), .ADDR(ADDR), .INTACK(INT_ACK), .MEMLD(MEMWT), .DOUT(DOUT), .DIN(DIN),
    .CLOCK(CLOCK), .reg0(out_5), .reg1(out_6), .reg2(out_7), .reg3(out_8), .reg4(out_9), .reg5(out_10),
    .reg6(out_11), .reg7(out_12));
  Button_part u_BUTTON_1 (.out(BUTTON_1_out));
  Button u_button_1_dup2 (.CLOCK(CLOCK), .OUT(BUTTON_1), .IN(BUTTON_1_out), .RESET(comparator_1_eq));
  // Probe on BUTTON_1
  Comparator #(.width(12)) comparator_1 (.a(12'ha08), .b(ADDR), .eq(comparator_1_eq));  // open: gt, lt
  Button_part u_BUTTON_2 (.out(BUTTON_2_out));
  Button u_button_2_dup2 (.CLOCK(CLOCK), .OUT(BUTTON_2), .IN(BUTTON_2_out), .RESET(comparator_2_eq));
  Comparator #(.width(12)) comparator_2 (.a(12'ha06), .b(ADDR), .eq(comparator_2_eq));  // open: gt, lt
  Comparator #(.width(12)) comparator_3 (
    .a(12'ha10), .b(ADDR), .gt(comparator_3_gt), .eq(comparator_3_eq), .lt(comparator_3_lt));
  // Probe on BUTTON_2
  // Probe on ADDR
  _1bit_register u_1bit_register_1 (.DATA(1'b1), .CLK(CLOCK), .LOAD(1'b1), .OUT(n1bit_register_1_out));
  Multiplexer #(.width(12), .enable("false")) multiplexer_1 (
    .in0({12{1'b0}}), .in1(ADDR), .out(multiplexer_1_out), .sel(n1bit_register_1_out));
  or or_1 (or_1_out, comparator_3_gt, comparator_3_lt);
  _16_bit_Register__SR u_16_bit_register_sr_1 (.Output(_7SEG_OUT), .Load(and_1_out), .in_1(DOUT), .Clock(CLOCK));
  and and_1 (and_1_out, comparator_3_eq, MEMWT);
  _16_bit_Register__SR u_16_bit_register_sr_2 (.Output(INPUT_1_t), .Load(1'b1), .in_1(INPUT_1), .Clock(CLOCK));
  and and_2 (and_2_out, MEMWT, or_1_out);
  RAM #(.addrWidth(12), .dataWidth(16), .bus("separate")) ram_1 (
    .addr(multiplexer_1_out), .din(DOUT), .data(ram_1_data), .str(and_2_out), .clk(CLOCK));  // open: sel, ld, clr
  _16_bit_Register__SR u_16_bit_register_sr_3 (.Output(INPUT_2_t), .Load(1'b1), .in_1(INPUT_2), .Clock(CLOCK));
  Comparator #(.width(12)) comparator_4 (.a(12'ha00), .b(ADDR), .eq(comparator_4_eq));  // open: gt, lt
  Multiplexer #(.width(16), .enable("false")) multiplexer_2 (
    .in0(ram_1_data), .in1(TIME), .out(multiplexer_2_out), .sel(comparator_4_eq));
  Comparator #(.width(12)) comparator_5 (.a(12'ha02), .b(ADDR), .eq(comparator_5_eq));  // open: gt, lt
  Comparator #(.width(12)) comparator_6 (.a(12'ha04), .b(ADDR), .eq(comparator_6_eq));  // open: gt, lt
  Comparator #(.width(12)) comparator_7 (.a(12'ha06), .b(ADDR), .eq(comparator_7_eq));  // open: gt, lt
  Comparator #(.width(12)) comparator_8 (.a(12'ha08), .b(ADDR), .eq(comparator_8_eq));  // open: gt, lt
  Comparator #(.width(12)) comparator_9 (.a(12'ha12), .b(ADDR), .eq(comparator_9_eq));  // open: gt, lt
  Multiplexer #(.width(16), .enable("false")) multiplexer_3 (
    .in0(multiplexer_2_out), .in1(INPUT_2_t), .out(multiplexer_3_out), .sel(comparator_5_eq));
  Multiplexer #(.width(16), .enable("false")) multiplexer_4 (
    .in0(multiplexer_3_out), .in1(INPUT_1_t), .out(multiplexer_4_out), .sel(comparator_6_eq));
  Multiplexer #(.width(16), .enable("false")) multiplexer_5 (
    .in0(multiplexer_4_out), .in1(BUTTON_2), .out(multiplexer_5_out), .sel(comparator_7_eq));
  Multiplexer #(.width(16), .enable("false")) multiplexer_6 (
    .in0(multiplexer_5_out), .in1(BUTTON_1), .out(multiplexer_6_out), .sel(comparator_8_eq));
  Multiplexer #(.width(16), .enable("false")) multiplexer_7 (
    .in0(multiplexer_6_out), .in1(SWITCH), .out(multiplexer_7_out), .sel(comparator_9_eq));
  Multiplexer #(.width(16), .enable("false")) multiplexer_8 (
    .in0(multiplexer_7_out), .in1(INT_DEVICE_ID), .out(DIN), .sel(INT_ACK));
  // Probe on DIN
  Hex_Digit_Display hex_digit_display_1 (.value(_7SEG_OUT[15:12]));  // open: dp
  Hex_Digit_Display hex_digit_display_2 (.value(_7SEG_OUT[11:8]));  // open: dp
  Hex_Digit_Display hex_digit_display_3 (.value(_7SEG_OUT[3:0]));  // open: dp
  Hex_Digit_Display hex_digit_display_4 (.value(_7SEG_OUT[7:4]));  // open: dp
endmodule

module \onların_pc  (
  input  [11:0] DATA,
  input  CLK,
  input  LOAD,
  input  PCINC,
  output [11:0] OUT
);

  wire or_1_out;
  wire [11:0] adder_1_out, multiplexer_1_out;

  or or_1 (or_1_out, LOAD, PCINC);
  Register #(.width(12)) register_1 (.D(multiplexer_1_out), .en(or_1_out), .Q(OUT), .clk(CLK));  // open: clr
  Multiplexer #(.select(2), .width(12), .enable("false")) multiplexer_1 (
    .in0(OUT), .in1(adder_1_out), .in2(DATA), .in3(OUT), .out(multiplexer_1_out), .sel({LOAD, PCINC}));
  Adder #(.width(12)) adder_1 (.a(12'h1), .b(OUT), .out(adder_1_out));  // open: cin, cout
endmodule

module doubledabble (
  input  [15:0] in_1,
  output [3:0] unit,
  output [3:0] tens,
  output [3:0] hundreds,
  output [3:0] thosands
);

  wire conditional_adder_1_out_5, conditional_adder_1_out_6, conditional_adder_1_out_7,
       conditional_adder_1_out_8, conditional_adder_2_out_5, conditional_adder_2_out_6,
       conditional_adder_2_out_7, conditional_adder_2_out_8, conditional_adder_3_out_5,
       conditional_adder_3_out_6, conditional_adder_3_out_7, conditional_adder_3_out_8,
       conditional_adder_4_out_5, conditional_adder_4_out_6, conditional_adder_4_out_7,
       conditional_adder_4_out_8, conditional_adder_5_out_5, conditional_adder_5_out_6,
       conditional_adder_5_out_7, conditional_adder_5_out_8, conditional_adder_6_out_5,
       conditional_adder_6_out_6, conditional_adder_6_out_7, conditional_adder_6_out_8,
       conditional_adder_7_out_5, conditional_adder_7_out_6, conditional_adder_7_out_7,
       conditional_adder_7_out_8, conditional_adder_8_out_5, conditional_adder_8_out_6,
       conditional_adder_8_out_7, conditional_adder_8_out_8, conditional_adder_9_out_5,
       conditional_adder_9_out_6, conditional_adder_9_out_7, conditional_adder_9_out_8,
       conditional_adder_10_out_5, conditional_adder_10_out_6, conditional_adder_10_out_7,
       conditional_adder_10_out_8, conditional_adder_11_out_5, conditional_adder_11_out_6,
       conditional_adder_11_out_7, conditional_adder_11_out_8, conditional_adder_12_out_5,
       conditional_adder_12_out_6, conditional_adder_12_out_7, conditional_adder_12_out_8,
       conditional_adder_13_out_5, conditional_adder_13_out_6, conditional_adder_13_out_7,
       conditional_adder_13_out_8, conditional_adder_14_out_5, conditional_adder_14_out_6,
       conditional_adder_14_out_7, conditional_adder_14_out_8, conditional_adder_15_out_5,
       conditional_adder_15_out_6, conditional_adder_15_out_7, conditional_adder_15_out_8,
       conditional_adder_16_out_5, conditional_adder_16_out_6, conditional_adder_16_out_7,
       conditional_adder_16_out_8, conditional_adder_17_out_5, conditional_adder_17_out_6,
       conditional_adder_17_out_7, conditional_adder_17_out_8, conditional_adder_18_out_5,
       conditional_adder_18_out_6, conditional_adder_18_out_7, conditional_adder_18_out_8,
       conditional_adder_19_out_5, conditional_adder_19_out_6, conditional_adder_19_out_7,
       conditional_adder_19_out_8, conditional_adder_20_out_5, conditional_adder_20_out_6,
       conditional_adder_20_out_7, conditional_adder_20_out_8, conditional_adder_21_out_5,
       conditional_adder_21_out_6, conditional_adder_21_out_7, conditional_adder_21_out_8,
       conditional_adder_22_out_5, conditional_adder_22_out_6, conditional_adder_22_out_7,
       conditional_adder_22_out_8, conditional_adder_23_out_5, conditional_adder_23_out_6,
       conditional_adder_23_out_7, conditional_adder_23_out_8, conditional_adder_24_out_5,
       conditional_adder_24_out_6, conditional_adder_24_out_7, conditional_adder_24_out_8,
       conditional_adder_25_out_5, conditional_adder_25_out_6, conditional_adder_25_out_7,
       conditional_adder_25_out_8, conditional_adder_26_out_5, conditional_adder_26_out_6,
       conditional_adder_26_out_7, conditional_adder_26_out_8, conditional_adder_27_out_8,
       conditional_adder_29_out_5, conditional_adder_29_out_6, conditional_adder_29_out_7,
       conditional_adder_29_out_8, conditional_adder_30_out_5, conditional_adder_30_out_6,
       conditional_adder_30_out_7, conditional_adder_30_out_8, conditional_adder_31_out_5,
       conditional_adder_31_out_6, conditional_adder_31_out_7, conditional_adder_31_out_8,
       conditional_adder_32_out_5, conditional_adder_32_out_6, conditional_adder_32_out_7,
       conditional_adder_32_out_8;

  conditional_adder conditional_adder_1 (
    .in_1(conditional_adder_9_out_8), .in_2(conditional_adder_8_out_8), .in_3(conditional_adder_7_out_8),
    .in_4(1'b0), .out_5(conditional_adder_1_out_5), .out_6(conditional_adder_1_out_6),
    .out_7(conditional_adder_1_out_7), .out_8(conditional_adder_1_out_8));
  conditional_adder conditional_adder_2 (
    .in_1(conditional_adder_13_out_8), .in_2(conditional_adder_11_out_8), .in_3(conditional_adder_1_out_8),
    .in_4(1'b0), .out_5(conditional_adder_2_out_5), .out_6(conditional_adder_2_out_6),
    .out_7(conditional_adder_2_out_7), .out_8(conditional_adder_2_out_8));
  conditional_adder conditional_adder_3 (
    .in_1(conditional_adder_16_out_8), .in_2(conditional_adder_2_out_5), .in_3(conditional_adder_2_out_6),
    .in_4(conditional_adder_2_out_7), .out_5(conditional_adder_3_out_5), .out_6(conditional_adder_3_out_6),
    .out_7(conditional_adder_3_out_7), .out_8(conditional_adder_3_out_8));
  conditional_adder conditional_adder_4 (
    .in_1(conditional_adder_19_out_8), .in_2(conditional_adder_3_out_8), .in_3(conditional_adder_2_out_8),
    .in_4(1'b0), .out_5(conditional_adder_4_out_5), .out_6(conditional_adder_4_out_6),
    .out_7(conditional_adder_4_out_7), .out_8(conditional_adder_4_out_8));
  conditional_adder conditional_adder_5 (
    .in_1(conditional_adder_22_out_8), .in_2(conditional_adder_4_out_5), .in_3(conditional_adder_4_out_6),
    .in_4(conditional_adder_4_out_7), .out_5(conditional_adder_5_out_5), .out_6(conditional_adder_5_out_6),
    .out_7(conditional_adder_5_out_7), .out_8(conditional_adder_5_out_8));
  conditional_adder conditional_adder_6 (
    .in_1(conditional_adder_24_out_8), .in_2(conditional_adder_5_out_5), .in_3(conditional_adder_5_out_6),
    .in_4(conditional_adder_5_out_7), .out_5(conditional_adder_6_out_5), .out_6(conditional_adder_6_out_6),
    .out_7(conditional_adder_6_out_7), .out_8(conditional_adder_6_out_8));
  conditional_adder conditional_adder_7 (
    .in_1(in_1[13]), .in_2(in_1[14]), .in_3(in_1[15]), .in_4(1'b0), .out_5(conditional_adder_7_out_5),
    .out_6(conditional_adder_7_out_6), .out_7(conditional_adder_7_out_7), .out_8(conditional_adder_7_out_8));
  conditional_adder conditional_adder_8 (
    .in_1(in_1[12]), .in_2(conditional_adder_7_out_5), .in_3(conditional_adder_7_out_6),
    .in_4(conditional_adder_7_out_7), .out_5(conditional_adder_8_out_5), .out_6(conditional_adder_8_out_6),
    .out_7(conditional_adder_8_out_7), .out_8(conditional_adder_8_out_8));
  conditional_adder conditional_adder_9 (
    .in_1(in_1[11]), .in_2(conditional_adder_8_out_5), .in_3(conditional_adder_8_out_6),
    .in_4(conditional_adder_8_out_7), .out_5(conditional_adder_9_out_5), .out_6(conditional_adder_9_out_6),
    .out_7(conditional_adder_9_out_7), .out_8(conditional_adder_9_out_8));
  conditional_adder conditional_adder_10 (
    .in_1(in_1[10]), .in_2(conditional_adder_9_out_5), .in_3(conditional_adder_9_out_6),
    .in_4(conditional_adder_9_out_7), .out_5(conditional_adder_10_out_5), .out_6(conditional_adder_10_out_6),
    .out_7(conditional_adder_10_out_7), .out_8(conditional_adder_10_out_8));
  conditional_adder conditional_adder_11 (
    .in_1(conditional_adder_10_out_8), .in_2(conditional_adder_1_out_5), .in_3(conditional_adder_1_out_6),
    .in_4(conditional_adder_1_out_7), .out_5(conditional_adder_11_out_5), .out_6(conditional_adder_11_out_6),
    .out_7(conditional_adder_11_out_7), .out_8(conditional_adder_11_out_8));
  conditional_adder conditional_adder_12 (
    .in_1(in_1[9]), .in_2(conditional_adder_10_out_5), .in_3(conditional_adder_10_out_6),
    .in_4(conditional_adder_10_out_7), .out_5(conditional_adder_12_out_5),
    .out_6(conditional_adder_12_out_6), .out_7(conditional_adder_12_out_7), .out_8(conditional_adder_12_out_8));
  conditional_adder conditional_adder_13 (
    .in_1(conditional_adder_12_out_8), .in_2(conditional_adder_11_out_5), .in_3(conditional_adder_11_out_6),
    .in_4(conditional_adder_11_out_7), .out_5(conditional_adder_13_out_5),
    .out_6(conditional_adder_13_out_6), .out_7(conditional_adder_13_out_7), .out_8(conditional_adder_13_out_8));
  conditional_adder conditional_adder_14 (
    .in_1(in_1[8]), .in_2(conditional_adder_12_out_5), .in_3(conditional_adder_12_out_6),
    .in_4(conditional_adder_12_out_7), .out_5(conditional_adder_14_out_5),
    .out_6(conditional_adder_14_out_6), .out_7(conditional_adder_14_out_7), .out_8(conditional_adder_14_out_8));
  conditional_adder conditional_adder_15 (
    .in_1(in_1[7]), .in_2(conditional_adder_14_out_5), .in_3(conditional_adder_14_out_6),
    .in_4(conditional_adder_14_out_7), .out_5(conditional_adder_15_out_5),
    .out_6(conditional_adder_15_out_6), .out_7(conditional_adder_15_out_7), .out_8(conditional_adder_15_out_8));
  conditional_adder conditional_adder_16 (
    .in_1(conditional_adder_14_out_8), .in_2(conditional_adder_13_out_5), .in_3(conditional_adder_13_out_6),
    .in_4(conditional_adder_13_out_7), .out_5(conditional_adder_16_out_5),
    .out_6(conditional_adder_16_out_6), .out_7(conditional_adder_16_out_7), .out_8(conditional_adder_16_out_8));
  conditional_adder conditional_adder_17 (
    .in_1(conditional_adder_15_out_8), .in_2(conditional_adder_16_out_5), .in_3(conditional_adder_16_out_6),
    .in_4(conditional_adder_16_out_7), .out_5(conditional_adder_17_out_5),
    .out_6(conditional_adder_17_out_6), .out_7(conditional_adder_17_out_7), .out_8(conditional_adder_17_out_8));
  conditional_adder conditional_adder_18 (
    .in_1(in_1[6]), .in_2(conditional_adder_15_out_5), .in_3(conditional_adder_15_out_6),
    .in_4(conditional_adder_15_out_7), .out_5(conditional_adder_18_out_5),
    .out_6(conditional_adder_18_out_6), .out_7(conditional_adder_18_out_7), .out_8(conditional_adder_18_out_8));
  conditional_adder conditional_adder_19 (
    .in_1(conditional_adder_17_out_8), .in_2(conditional_adder_3_out_5), .in_3(conditional_adder_3_out_6),
    .in_4(conditional_adder_3_out_7), .out_5(conditional_adder_19_out_5), .out_6(conditional_adder_19_out_6),
    .out_7(conditional_adder_19_out_7), .out_8(conditional_adder_19_out_8));
  conditional_adder conditional_adder_20 (
    .in_1(conditional_adder_18_out_8), .in_2(conditional_adder_17_out_5), .in_3(conditional_adder_17_out_6),
    .in_4(conditional_adder_17_out_7), .out_5(conditional_adder_20_out_5),
    .out_6(conditional_adder_20_out_6), .out_7(conditional_adder_20_out_7), .out_8(conditional_adder_20_out_8));
  conditional_adder conditional_adder_21 (
    .in_1(conditional_adder_29_out_8), .in_2(conditional_adder_20_out_5), .in_3(conditional_adder_20_out_6),
    .in_4(conditional_adder_20_out_7), .out_5(conditional_adder_21_out_5),
    .out_6(conditional_adder_21_out_6), .out_7(conditional_adder_21_out_7), .out_8(conditional_adder_21_out_8));
  conditional_adder conditional_adder_22 (
    .in_1(conditional_adder_20_out_8), .in_2(conditional_adder_19_out_5), .in_3(conditional_adder_19_out_6),
    .in_4(conditional_adder_19_out_7), .out_5(conditional_adder_22_out_5),
    .out_6(conditional_adder_22_out_6), .out_7(conditional_adder_22_out_7), .out_8(conditional_adder_22_out_8));
  conditional_adder conditional_adder_23 (
    .in_1(conditional_adder_30_out_8), .in_2(conditional_adder_21_out_5), .in_3(conditional_adder_21_out_6),
    .in_4(conditional_adder_21_out_7), .out_5(conditional_adder_23_out_5),
    .out_6(conditional_adder_23_out_6), .out_7(conditional_adder_23_out_7), .out_8(conditional_adder_23_out_8));
  conditional_adder conditional_adder_24 (
    .in_1(conditional_adder_21_out_8), .in_2(conditional_adder_22_out_5), .in_3(conditional_adder_22_out_6),
    .in_4(conditional_adder_22_out_7), .out_5(conditional_adder_24_out_5),
    .out_6(conditional_adder_24_out_6), .out_7(conditional_adder_24_out_7), .out_8(conditional_adder_24_out_8));
  conditional_adder conditional_adder_25 (
    .in_1(conditional_adder_31_out_8), .in_2(conditional_adder_23_out_5), .in_3(conditional_adder_23_out_6),
    .in_4(conditional_adder_23_out_7), .out_5(conditional_adder_25_out_5),
    .out_6(conditional_adder_25_out_6), .out_7(conditional_adder_25_out_7), .out_8(conditional_adder_25_out_8));
  conditional_adder conditional_adder_26 (
    .in_1(conditional_adder_23_out_8), .in_2(conditional_adder_24_out_5), .in_3(conditional_adder_24_out_6),
    .in_4(conditional_adder_24_out_7), .out_5(conditional_adder_26_out_5),
    .out_6(conditional_adder_26_out_6), .out_7(conditional_adder_26_out_7), .out_8(conditional_adder_26_out_8));
  conditional_adder conditional_adder_27 (
    .in_1(conditional_adder_26_out_8), .in_2(conditional_adder_6_out_5), .in_3(conditional_adder_6_out_6),
    .in_4(conditional_adder_6_out_7), .out_5(thosands[1]), .out_6(thosands[2]), .out_7(thosands[3]),
    .out_8(conditional_adder_27_out_8));
  conditional_adder conditional_adder_28 (
    .in_1(conditional_adder_25_out_8), .in_2(conditional_adder_26_out_5), .in_3(conditional_adder_26_out_6),
    .in_4(conditional_adder_26_out_7), .out_5(hundreds[1]), .out_6(hundreds[2]), .out_7(hundreds[3]),
    .out_8(thosands[0]));
  conditional_adder conditional_adder_29 (
    .in_1(in_1[5]), .in_2(conditional_adder_18_out_5), .in_3(conditional_adder_18_out_6),
    .in_4(conditional_adder_18_out_7), .out_5(conditional_adder_29_out_5),
    .out_6(conditional_adder_29_out_6), .out_7(conditional_adder_29_out_7), .out_8(conditional_adder_29_out_8));
  conditional_adder conditional_adder_30 (
    .in_1(in_1[4]), .in_2(conditional_adder_29_out_5), .in_3(conditional_adder_29_out_6),
    .in_4(conditional_adder_29_out_7), .out_5(conditional_adder_30_out_5),
    .out_6(conditional_adder_30_out_6), .out_7(conditional_adder_30_out_7), .out_8(conditional_adder_30_out_8));
  conditional_adder conditional_adder_31 (
    .in_1(in_1[3]), .in_2(conditional_adder_30_out_5), .in_3(conditional_adder_30_out_6),
    .in_4(conditional_adder_30_out_7), .out_5(conditional_adder_31_out_5),
    .out_6(conditional_adder_31_out_6), .out_7(conditional_adder_31_out_7), .out_8(conditional_adder_31_out_8));
  conditional_adder conditional_adder_32 (
    .in_1(in_1[2]), .in_2(conditional_adder_31_out_5), .in_3(conditional_adder_31_out_6),
    .in_4(conditional_adder_31_out_7), .out_5(conditional_adder_32_out_5),
    .out_6(conditional_adder_32_out_6), .out_7(conditional_adder_32_out_7), .out_8(conditional_adder_32_out_8));
  conditional_adder conditional_adder_33 (
    .in_1(conditional_adder_32_out_8), .in_2(conditional_adder_25_out_5), .in_3(conditional_adder_25_out_6),
    .in_4(conditional_adder_25_out_7), .out_5(tens[1]), .out_6(tens[2]), .out_7(tens[3]), .out_8(hundreds[0]));
  conditional_adder conditional_adder_34 (
    .in_1(in_1[1]), .in_2(conditional_adder_32_out_5), .in_3(conditional_adder_32_out_6),
    .in_4(conditional_adder_32_out_7), .out_5(unit[1]), .out_6(unit[2]), .out_7(unit[3]), .out_8(tens[0]));
  Hex_Digit_Display hex_digit_display_1 (.value(thosands));  // open: dp
  Hex_Digit_Display hex_digit_display_2 (.value(tens));  // open: dp
  Hex_Digit_Display hex_digit_display_3 (.value(hundreds));  // open: dp
  Hex_Digit_Display hex_digit_display_4 (.value({unit[3:1], in_1[0]}));  // open: dp

  assign unit[0] = in_1[0];
endmodule

module conditional_adder (
  input  in_1,
  input  in_2,
  input  in_3,
  input  in_4,
  output out_5,
  output out_6,
  output out_7,
  output out_8
);

  wire comparator_1_gt;
  wire [3:0] adder_1_out;

  Adder #(.width(4)) adder_1 (.a({in_4, in_3, in_2, in_1}), .b(4'b0011), .out(adder_1_out));  // open: cin, cout
  Comparator #(.width(4)) comparator_1 (
    .a({in_4, in_3, in_2, in_1}), .b(4'b0100), .gt(comparator_1_gt));  // open: eq, lt
  Multiplexer #(.width(4), .enable("false")) multiplexer_1 (
    .in0({in_4, in_3, in_2, in_1}), .in1(adder_1_out), .out({out_8, out_7, out_6, out_5}),
    .sel(comparator_1_gt));
endmodule
